# Fritzing sketch dispDistance (saved by Fritzing 0.9.3b)
breadboards: 1

parts:
  Raspberry_Pi_1 = Raspberry Pi 3 [part_number=RPI-3-V1.2]
  OLED_I2C1 = OLED 128x64 I2C Monochrome Display
  パーツ1 = Adafruit VL530X Time of Flight Distance Sensor [part_number="Adafruit #3317"]

nets:
  3V3: Raspberry_Pi_1.3v3, OLED_I2C1.VDD, パーツ1.VCC
  N1: Raspberry_Pi_1.GPIO2, OLED_I2C1.SDA, パーツ1.SDA
  N2: Raspberry_Pi_1.GPIO3, OLED_I2C1.SCK, パーツ1.SCL
  GND: Raspberry_Pi_1.GND, OLED_I2C1.GND, パーツ1.GND

custom parts:
  Adafruit VL530X Time of Flight Distance Sensor: The VL53L0X is a Time of Flight distance sensor like no other you've used! The sensor contains a very tiny invisible laser source, and a matching sensor. The VL53L0X can detect the "time of flight", or how long the light has taken to bounce back to the sensor. Since it uses a very narrow light source, it is good for determining distance of only the surface directly in front of it. Unlike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
